// Logisim project 1.circ as structural Verilog: 1 circuit, main circuit introduction
module introduction (
  input  A,
  input  B,
  input  C,
  input  D,
  output f,
  output g
);

  wire and_1_out, and_2_out, and_3_out, and_4_out, and_5_out, and_6_out, and_7_out, notA, notB, notC, notD;

  not not_1 (notA, A);
  not not_2 (notB, B);
  not not_3 (notC, C);
  and and_1 (and_1_out, A, C);
  not not_4 (notD, D);
  and and_2 (and_2_out, B, notD);
  and and_3 (and_3_out, notC, notD);
  or or_1 (f, and_1_out, and_2_out, and_3_out);
  and and_4 (and_4_out, A, B, C, D);
  and and_5 (and_5_out, B, D, notC);
  and and_6 (and_6_out, notA, notD);
  and and_7 (and_7_out, A, D, notB);
  or or_2 (g, and_4_out, and_5_out, and_6_out, and_7_out);
endmodule
