// Logisim project 2.circ as structural Verilog: 1 circuit, main circuit minterm
module minterm (
  input  [3:0] fourbitinput,
  output h
);

  wire not_1_out;

  not not_1 (not_1_out, fourbitinput[0]);
  and and_1 (h, fourbitinput[3], fourbitinput[2], fourbitinput[1], not_1_out);

  // Other names for the same wires on the sheet: D = fourbitinput[0]; C = fourbitinput[1]; B = fourbitinput[2];
  //   A = fourbitinput[3]
endmodule
