// Logisim project 6.circ as structural Verilog: 1 circuit, main circuit multiplexor
module multiplexor (
  input  [2:0] inputzero,
  input  [2:0] inputone,
  input  [2:0] inputtwo,
  input  [2:0] inputthree,
  input  [1:0] selector,
  output [2:0] muxoutput
);

  wire [2:0] and_1_out, and_2_out, and_3_out, and_4_out, not_1_out, not_2_out, s0, s1;

  assign not_1_out = ~s0;  // NOT_Gate not_1, 3 bits wide
  assign not_2_out = ~s1;  // NOT_Gate not_2, 3 bits wide
  assign s0 = {{2{selector[0]}}, selector[0]};  // Bit_Extender bit_extender_1
  assign s1 = {{2{selector[1]}}, selector[1]};  // Bit_Extender bit_extender_2
  assign and_1_out = not_2_out & inputzero & not_1_out;  // AND_Gate and_1, 3 bits wide
  assign and_2_out = s0 & inputone & not_2_out;  // AND_Gate and_2, 3 bits wide
  assign and_3_out = s1 & inputtwo & not_1_out;  // AND_Gate and_3, 3 bits wide
  assign and_4_out = s1 & inputthree & s0;  // AND_Gate and_4, 3 bits wide
  assign muxoutput = and_1_out | and_2_out | and_3_out | and_4_out;  // OR_Gate or_1, 3 bits wide

  // Other names for the same wires on the sheet: i0[2:0] = inputzero; i1[2:0] = inputone; i2[2:0] = inputtwo;
  //   i3[2:0] = inputthree; O[2:0] = muxoutput; s[1:0] = selector
endmodule
