// Logisim project extracredit.circ as structural Verilog: 2 circuits, main circuit tripledigit
module tripledigit (
  input  [9:0] thousand,
  output [6:0] hundreds,
  output [6:0] tens,
  output [6:0] ones
);

  wire and_1_out, and_2_out, and_3_out, and_4_out, and_5_out, and_6_out, and_7_out, and_8_out, and_9_out,
       and_10_out, and_11_out, and_12_out, and_13_out, and_14_out, and_15_out, and_16_out, i0, i1, i2, i3,
       not_1_out, not_2_out, not_3_out, not_4_out, not_5_out, not_6_out, not_7_out, not_8_out, not_9_out,
       not_10_out, not_11_out, not_12_out, not_13_out, not_14_out, not_15_out, not_16_out, not_17_out,
       not_18_out, not_19_out, not_20_out;

  Bit_Extender #(.in_width(10), .out_width(4)) bit_extender_1 (.in(thousand), .out({i3, i2, i1, i0}));
  Bit_Extender #(.in_width(10), .out_width(4)) bit_extender_2 (.in(thousand), .out({i3, i2, i1, i0}));
  Bit_Extender #(.in_width(10), .out_width(4)) bit_extender_3 (.in(thousand), .out({i3, i2, i1, i0}));
  not not_1 (not_1_out, i2);
  not not_2 (not_2_out, i1);
  not not_3 (not_3_out, i0);
  and and_1 (and_1_out, i2, i0);
  not not_4 (not_4_out, i2);
  and and_2 (and_2_out, not_4_out, not_5_out);
  not not_5 (not_5_out, i0);
  and and_3 (and_3_out, not_2_out, not_3_out);
  and and_4 (and_4_out, i1, i0);
  not not_6 (not_6_out, i1);
  not not_7 (not_7_out, i3);
  not not_8 (not_8_out, i2);
  not not_9 (not_9_out, i1);
  not not_10 (not_10_out, i0);
  or or_1 (hundreds[2], i2, not_6_out, i0);
  and and_5 (and_5_out, not_8_out, not_9_out, not_10_out);
  and and_6 (and_6_out, i2, not_9_out, i0);
  and and_7 (and_7_out, not_10_out, i1);
  and and_8 (and_8_out, not_7_out, not_8_out, i1);
  or or_2 (hundreds[0], i3, i1, and_1_out, and_2_out);
  or or_3 (hundreds[1], not_1_out, and_3_out, and_4_out);
  or or_4 (hundreds[3], i3, and_5_out, and_6_out, and_7_out, and_8_out);
  _7_Segment_Display u_7_segment_display_1 (
    .g(hundreds[0]), .f(hundreds[1]), .a(hundreds[2]), .b(hundreds[3]), .e(hundreds[4]), .d(hundreds[5]),
    .c(hundreds[6]));  // open: dp
  not not_11 (not_11_out, i2);
  not not_12 (not_12_out, i1);
  not not_13 (not_13_out, i0);
  not not_14 (not_14_out, i3);
  not not_15 (not_15_out, i1);
  not not_16 (not_16_out, i0);
  not not_17 (not_17_out, i3);
  not not_18 (not_18_out, i2);
  not not_19 (not_19_out, i1);
  not not_20 (not_20_out, i0);
  and and_9 (and_9_out, not_13_out, i1);
  and and_10 (and_10_out, not_11_out, not_12_out, not_13_out);
  _7_Segment_Display u_7_segment_display_2 (
    .g(hundreds[0]), .f(hundreds[1]), .a(hundreds[2]), .b(hundreds[3]), .e(hundreds[4]), .d(hundreds[5]),
    .c(hundreds[6]));  // open: dp
  and and_11 (and_11_out, not_15_out, not_16_out);
  and and_12 (and_12_out, not_14_out, i2, not_15_out);
  and and_13 (and_13_out, i2, i1, not_16_out);
  and and_14 (and_14_out, i2, not_19_out);
  and and_15 (and_15_out, i1, not_20_out);
  and and_16 (and_16_out, i1, not_17_out, not_18_out);
  _7_Segment_Display u_7_segment_display_3 (
    .g(hundreds[0]), .f(hundreds[1]), .a(hundreds[2]), .b(hundreds[3]), .e(hundreds[4]), .d(hundreds[5]),
    .c(hundreds[6]));  // open: dp
  or or_5 (hundreds[4], and_9_out, and_10_out);
  or or_6 (hundreds[5], i3, and_11_out, and_12_out, and_13_out);
  or or_7 (hundreds[6], i3, and_14_out, and_15_out, and_16_out);

  assign ones = hundreds;
  assign tens = hundreds;

  // Other names for the same wires on the sheet: a = hundreds[0]; h[6:0] = hundreds; o[6:0] = hundreds;
  //   t[6:0] = hundreds; b = hundreds[1]; c = hundreds[2]; d = hundreds[3]; e = hundreds[4]; f = hundreds[5];
  //   g = hundreds[6]
endmodule

module singledigit (
  input  [3:0] i,
  output a,
  output b,
  output c,
  output d,
  output e,
  output f,
  output g
);

  wire and_1_out, and_2_out, and_3_out, and_4_out, and_5_out, and_6_out, and_7_out, and_8_out, and_9_out,
       and_10_out, and_11_out, and_12_out, and_13_out, and_14_out, and_15_out, and_16_out, not_1_out,
       not_2_out, not_3_out, not_4_out, not_5_out, not_6_out, not_7_out, not_8_out, not_9_out, not_10_out,
       not_11_out, not_12_out, not_13_out, not_14_out, not_15_out, not_16_out, not_17_out, not_18_out,
       not_19_out, not_20_out;

  _7_Segment_Display u_7_segment_display_1 (.g(a), .f(b), .a(c), .b(d), .e(e), .d(f), .c(g));  // open: dp
  not not_1 (not_1_out, i[2]);
  not not_2 (not_2_out, i[1]);
  not not_3 (not_3_out, i[0]);
  not not_4 (not_4_out, i[1]);
  and and_1 (and_1_out, i[2], i[0]);
  not not_5 (not_5_out, i[2]);
  and and_2 (and_2_out, not_5_out, not_6_out);
  not not_6 (not_6_out, i[0]);
  and and_3 (and_3_out, not_2_out, not_3_out);
  and and_4 (and_4_out, i[1], i[0]);
  not not_7 (not_7_out, i[3]);
  not not_8 (not_8_out, i[2]);
  not not_9 (not_9_out, i[1]);
  not not_10 (not_10_out, i[0]);
  not not_11 (not_11_out, i[2]);
  not not_12 (not_12_out, i[1]);
  not not_13 (not_13_out, i[0]);
  not not_14 (not_14_out, i[3]);
  not not_15 (not_15_out, i[1]);
  not not_16 (not_16_out, i[0]);
  not not_17 (not_17_out, i[3]);
  not not_18 (not_18_out, i[2]);
  not not_19 (not_19_out, i[1]);
  not not_20 (not_20_out, i[0]);
  or or_1 (c, i[2], not_4_out, i[0]);
  and and_5 (and_5_out, not_8_out, not_9_out, not_10_out);
  and and_6 (and_6_out, i[2], not_9_out, i[0]);
  and and_7 (and_7_out, not_10_out, i[1]);
  and and_8 (and_8_out, not_7_out, not_8_out, i[1]);
  and and_9 (and_9_out, not_13_out, i[1]);
  and and_10 (and_10_out, not_11_out, not_12_out, not_13_out);
  and and_11 (and_11_out, not_15_out, not_16_out);
  and and_12 (and_12_out, not_14_out, i[2], not_15_out);
  and and_13 (and_13_out, i[2], i[1], not_16_out);
  and and_14 (and_14_out, i[2], not_19_out);
  and and_15 (and_15_out, i[1], not_20_out);
  and and_16 (and_16_out, i[1], not_17_out, not_18_out);
  or or_2 (a, i[3], i[1], and_1_out, and_2_out);
  or or_3 (b, not_1_out, and_3_out, and_4_out);
  or or_4 (d, i[3], and_5_out, and_6_out, and_7_out, and_8_out);
  or or_5 (e, and_9_out, and_10_out);
  or or_6 (f, i[3], and_11_out, and_12_out, and_13_out);
  or or_7 (g, i[3], and_14_out, and_15_out, and_16_out);
endmodule
