// Logisim project 1.circ as structural Verilog: 1 circuit, main circuit muxfunction
module muxfunction (
  input  [3:0] fourbitinput,
  output f
);

  wire abncnd, multiplexer_6_out, multiplexer_7_out, multiplexer_8_out, multiplexer_9_out,
       multiplexer_13_out, multiplexer_14_out, na, nanbnc, nancd, nb, nbd, nc, nd;

  Multiplexer #(.enable("false")) multiplexer_1 (.in0(1'b1), .in1(1'b0), .out(na), .sel(fourbitinput[3]));
  Multiplexer #(.enable("false")) multiplexer_2 (.in0(1'b1), .in1(1'b0), .out(nb), .sel(fourbitinput[2]));
  Multiplexer #(.enable("false")) multiplexer_3 (.in0(1'b1), .in1(1'b0), .out(nc), .sel(fourbitinput[1]));
  Multiplexer #(.enable("false")) multiplexer_4 (.in0(1'b1), .in1(1'b0), .out(nd), .sel(fourbitinput[0]));
  Multiplexer #(.enable("false")) multiplexer_5 (.in0(1'b0), .in1(nb), .out(nbd), .sel(fourbitinput[0]));
  Multiplexer #(.enable("false")) multiplexer_6 (
    .in0(1'b0), .in1(fourbitinput[3]), .out(multiplexer_6_out), .sel(fourbitinput[2]));
  Multiplexer #(.enable("false")) multiplexer_7 (.in0(1'b0), .in1(nc), .out(multiplexer_7_out), .sel(nd));
  Multiplexer #(.enable("false")) multiplexer_8 (.in0(1'b0), .in1(na), .out(multiplexer_8_out), .sel(nc));
  Multiplexer #(.enable("false")) multiplexer_9 (.in0(1'b0), .in1(na), .out(multiplexer_9_out), .sel(nb));
  Multiplexer #(.enable("false")) multiplexer_10 (
    .in0(1'b0), .in1(multiplexer_6_out), .out(abncnd), .sel(multiplexer_7_out));
  Multiplexer #(.enable("false")) multiplexer_11 (
    .in0(1'b0), .in1(multiplexer_8_out), .out(nancd), .sel(fourbitinput[0]));
  Multiplexer #(.enable("false")) multiplexer_12 (.in0(1'b0), .in1(multiplexer_9_out), .out(nanbnc), .sel(nc));
  Multiplexer #(.enable("false")) multiplexer_13 (.in0(nbd), .in1(1'b1), .out(multiplexer_13_out), .sel(abncnd));
  Multiplexer #(.enable("false")) multiplexer_14 (.in0(nancd), .in1(1'b1), .out(multiplexer_14_out), .sel(nanbnc));
  Multiplexer #(.enable("false")) multiplexer_15 (
    .in0(multiplexer_13_out), .in1(1'b1), .out(f), .sel(multiplexer_14_out));

  // Other names for the same wires on the sheet: d = fourbitinput[0]; c = fourbitinput[1]; b = fourbitinput[2];
  //   a = fourbitinput[3]
endmodule
