// Logisim project 2.circ as structural Verilog: 1 circuit, main circuit decoderfunction
module decoderfunction (
  input  [3:0] fourbitinput,
  output g
);

  wire decoder_1_out1, decoder_1_out2, decoder_1_out5, decoder_1_out8, decoder_1_out13, decoder_1_out14,
       decoder_1_out15;

  Decoder #(.select(4)) decoder_1 (
    .out1(decoder_1_out1), .out2(decoder_1_out2), .out5(decoder_1_out5), .out8(decoder_1_out8),
    .out13(decoder_1_out13), .out14(decoder_1_out14), .out15(decoder_1_out15), .sel(fourbitinput), .en(1'b1));  // open: out0, out3, out4, out6, out7, out9, out10, out11, out12
  or or_1 (g, decoder_1_out1, decoder_1_out2, decoder_1_out5, decoder_1_out15, decoder_1_out8, decoder_1_out13, decoder_1_out14);

  // Other names for the same wires on the sheet: d = fourbitinput[0]; c = fourbitinput[1]; b = fourbitinput[2];
  //   a = fourbitinput[3]
endmodule
