// Logisim project 3.circ as structural Verilog: 1 circuit, main circuit bitcounting
module bitcounting (
  input  [11:0] twelvebitinput,
  output [3:0] zeroes
);

  wire [11:0] not_1_out;

  assign not_1_out = ~twelvebitinput;  // NOT_Gate not_1, 12 bits wide
  BitAdder #(.width(1)) bitadder_1 (
    .in0(not_1_out[11]), .in1(not_1_out[10]), .in2(not_1_out[9]), .in3(not_1_out[8]), .in4(not_1_out[7]),
    .in5(not_1_out[6]), .in6(not_1_out[5]), .in7(not_1_out[4]), .in8(not_1_out[3]), .in9(not_1_out[2]),
    .in10(not_1_out[1]), .in11(not_1_out[0]), .out(zeroes));

  // Other names for the same wires on the sheet: f[3:0] = zeroes
endmodule
