// Logisim project 4.circ as structural Verilog: 1 circuit, main circuit comparison
module comparison (
  input  [7:0] inputa,
  input  [7:0] inputb,
  output areequal
);

  wire xnor_1_out, xnor_2_out, xnor_3_out, xnor_4_out, xnor_5_out, xnor_6_out, xnor_7_out, xnor_8_out;

  xnor xnor_1 (xnor_1_out, inputa[7], inputb[7]);
  xnor xnor_2 (xnor_2_out, inputa[6], inputb[6]);
  xnor xnor_3 (xnor_3_out, inputa[5], inputb[5]);
  xnor xnor_4 (xnor_4_out, inputa[4], inputb[4]);
  xnor xnor_5 (xnor_5_out, inputa[3], inputb[3]);
  xnor xnor_6 (xnor_6_out, inputa[2], inputb[2]);
  xnor xnor_7 (xnor_7_out, inputa[1], inputb[1]);
  xnor xnor_8 (xnor_8_out, inputa[0], inputb[0]);
  and and_1 (areequal, xnor_1_out, xnor_2_out, xnor_3_out, xnor_4_out, xnor_5_out, xnor_6_out, xnor_7_out, xnor_8_out);

  // Other names for the same wires on the sheet: f = areequal; a7 = inputa[0]; a6 = inputa[1]; a5 = inputa[2];
  //   a4 = inputa[3]; a3 = inputa[4]; a2 = inputa[5]; a1 = inputa[6]; a0 = inputa[7]; b7 = inputb[0]; b6 = inputb[1];
  //   b5 = inputb[2]; b4 = inputb[3]; b3 = inputb[4]; b2 = inputb[5]; b1 = inputb[6]; b0 = inputb[7]
endmodule
