// Logisim project 6.circ as structural Verilog: 1 circuit, main circuit cla
module cla (
  input  [3:0] inputa,
  input  [3:0] inputb,
  input  carryin,
  output [3:0] carryout,
  output [3:0] generator,
  output [3:0] propagator
);

  wire and_5_out, and_6_out, and_7_out, and_8_out;

  and and_1 (generator[0], inputa[0], inputb[0]);
  and and_2 (generator[1], inputa[1], inputb[1]);
  and and_3 (generator[2], inputa[2], inputb[2]);
  and and_4 (generator[3], inputa[3], inputb[3]);
  xor xor_1 (propagator[0], inputa[0], inputb[0]);
  xor xor_2 (propagator[1], inputa[1], inputb[1]);
  xor xor_3 (propagator[2], inputb[2], inputa[2]);
  xor xor_4 (propagator[3], inputa[3], inputb[3]);
  and and_5 (and_5_out, propagator[0], carryin);
  and and_6 (and_6_out, propagator[1], carryout[0]);
  or or_1 (carryout[0], and_5_out, generator[0]);
  or or_2 (carryout[1], and_6_out, generator[1]);
  and and_7 (and_7_out, propagator[2], carryout[1]);
  and and_8 (and_8_out, propagator[3], carryout[2]);
  or or_3 (carryout[2], and_7_out, generator[2]);
  or or_4 (carryout[3], and_8_out, generator[3]);

  // Other names for the same wires on the sheet: C[3:0] = carryout; C1 = carryout[0]; C2 = carryout[1];
  //   C3 = carryout[2]; C4 = carryout[3]; C0 = carryin; G[3:0] = generator; G0 = generator[0]; G1 = generator[1];
  //   G2 = generator[2]; G3 = generator[3]; a0 = inputa[0]; a1 = inputa[1]; a2 = inputa[2]; a3 = inputa[3];
  //   b0 = inputb[0]; b1 = inputb[1]; b2 = inputb[2]; b3 = inputb[3]; P[3:0] = propagator; P0 = propagator[0];
  //   P1 = propagator[1]; P2 = propagator[2]; P3 = propagator[3]
endmodule
