// Logisim project 7.circ as structural Verilog: 1 circuit, main circuit alu
module alu (
  input  [3:0] inputa,
  input  [3:0] inputb,
  input  [2:0] operation,
  output [3:0] aluout
);

  wire and_1_out, and_2_out, and_3_out, and_4_out, and_9_out, and_10_out, and_11_out, and_12_out, and_17_out,
       and_18_out, and_19_out, bn0, bn1, bn2, bn3, C1, C2, C3, C4, Cn1, Cn2, Cn3, G0, G1, G2, G3, Gn0, Gn1,
       Gn2, Gn3, not_1_out, not_2_out, not_7_out, not_8_out, not_9_out, not_10_out, not_11_out, not_12_out,
       or_5_out, or_9_out, or_10_out, or_11_out, P0, P1, P2, P3, Pn0, Pn1, Pn2, Pn3, xor_5_out, xor_6_out,
       xor_7_out, xor_8_out, xor_13_out, xor_14_out, xor_15_out, xor_16_out, xor_17_out, xor_18_out,
       xor_19_out, xor_20_out, xor_21_out, xor_22_out, xor_23_out, xor_24_out;

  and and_1 (and_1_out, P0, 1'b0);
  and and_2 (and_2_out, P1, C1);
  and and_3 (and_3_out, Pn0, 1'b1);
  and and_4 (and_4_out, Pn1, Cn1);
  not not_1 (not_1_out, inputa[0]);
  not not_2 (not_2_out, inputb[0]);
  or or_1 (C1, and_1_out, G0);
  or or_2 (C2, and_2_out, G1);
  or or_3 (Cn1, and_3_out, Gn0);
  or or_4 (Cn2, and_4_out, Gn1);
  and and_5 (G0, inputa[0], inputb[0]);
  and and_6 (G1, inputa[1], inputb[1]);
  and and_7 (G2, inputa[2], inputb[2]);
  and and_8 (G3, inputa[3], inputb[3]);
  xor xor_1 (P0, inputa[0], inputb[0]);
  xor xor_2 (P1, inputa[1], inputb[1]);
  xor xor_3 (P2, inputb[2], inputa[2]);
  xor xor_4 (P3, inputa[3], inputb[3]);
  xor xor_5 (xor_5_out, inputa[0], not_2_out);
  and and_9 (and_9_out, inputa[0], inputb[0]);
  or or_5 (or_5_out, inputa[0], inputb[0]);
  xor xor_6 (xor_6_out, inputa[0], inputb[0]);
  xor xor_7 (xor_7_out, xor_6_out, 1'b0);
  and and_10 (and_10_out, P2, C2);
  and and_11 (and_11_out, P3, C3);
  and and_12 (and_12_out, Pn2, Cn2);
  or or_6 (C3, and_10_out, G2);
  or or_7 (C4, and_11_out, G3);
  or or_8 (Cn3, and_12_out, Gn2);
  xor xor_8 (xor_8_out, xor_5_out, 1'b1);
  Multiplexer #(.select(3), .enable("false")) multiplexer_1 (
    .in0(and_9_out), .in1(not_2_out), .in2(or_5_out), .in3(xor_8_out), .in4(xor_6_out), .in5(not_1_out),
    .in6(xor_7_out), .out(aluout[0]), .sel(operation));  // open: in7
  not not_3 (bn0, inputb[0]);
  not not_4 (bn1, inputb[1]);
  not not_5 (bn2, inputb[2]);
  not not_6 (bn3, inputb[3]);
  not not_7 (not_7_out, inputa[1]);
  not not_8 (not_8_out, inputb[1]);
  not not_9 (not_9_out, inputa[2]);
  not not_10 (not_10_out, inputb[2]);
  and and_13 (Gn0, inputa[0], bn0);
  and and_14 (Gn1, inputa[1], bn1);
  and and_15 (Gn2, inputa[2], bn2);
  and and_16 (Gn3, inputa[3], bn3);
  xor xor_9 (Pn0, inputa[0], bn0);
  xor xor_10 (Pn1, inputa[1], bn1);
  xor xor_11 (Pn2, bn2, inputa[2]);
  xor xor_12 (Pn3, inputa[3], bn3);
  not not_11 (not_11_out, inputa[3]);
  not not_12 (not_12_out, inputb[3]);
  and and_17 (and_17_out, inputa[1], inputb[1]);
  or or_9 (or_9_out, inputa[1], inputb[1]);
  xor xor_13 (xor_13_out, inputa[2], not_10_out);
  and and_18 (and_18_out, inputa[2], inputb[2]);
  or or_10 (or_10_out, inputa[2], inputb[2]);
  xor xor_14 (xor_14_out, inputa[2], inputb[2]);
  xor xor_15 (xor_15_out, inputa[1], not_8_out);
  xor xor_16 (xor_16_out, inputa[1], inputb[1]);
  xor xor_17 (xor_17_out, xor_16_out, C1);
  xor xor_18 (xor_18_out, xor_14_out, C2);
  xor xor_19 (xor_19_out, inputa[3], not_12_out);
  and and_19 (and_19_out, inputa[3], inputb[3]);
  or or_11 (or_11_out, inputa[3], inputb[3]);
  xor xor_20 (xor_20_out, inputa[3], inputb[3]);
  xor xor_21 (xor_21_out, xor_20_out, C3);
  xor xor_22 (xor_22_out, xor_15_out, Cn1);
  xor xor_23 (xor_23_out, xor_13_out, Cn2);
  Multiplexer #(.select(3), .enable("false")) multiplexer_2 (
    .in0(and_17_out), .in1(not_8_out), .in2(or_9_out), .in3(xor_22_out), .in4(xor_16_out), .in5(not_7_out),
    .in6(xor_17_out), .out(aluout[1]), .sel(operation));  // open: in7
  Multiplexer #(.select(3), .enable("false")) multiplexer_3 (
    .in0(and_18_out), .in1(not_10_out), .in2(or_10_out), .in3(xor_23_out), .in4(xor_14_out), .in5(not_9_out),
    .in6(xor_18_out), .out(aluout[2]), .sel(operation));  // open: in7
  xor xor_24 (xor_24_out, xor_19_out, Cn3);
  Multiplexer #(.select(3), .enable("false")) multiplexer_4 (
    .in0(and_19_out), .in1(not_12_out), .in2(or_11_out), .in3(xor_24_out), .in4(xor_20_out),
    .in5(not_11_out), .in6(xor_21_out), .out(aluout[3]), .sel(operation));  // open: in7

  // Other names for the same wires on the sheet: O1 = aluout[0]; O2 = aluout[1]; O3 = aluout[2]; O4 = aluout[3];
  //   a0 = inputa[0]; a1 = inputa[1]; a2 = inputa[2]; a3 = inputa[3]; b0 = inputb[0]; b1 = inputb[1]; b2 = inputb[2];
  //   b3 = inputb[3]; Op[2:0] = operation
endmodule
