// Logisim project 8.circ as structural Verilog: 1 circuit, main circuit errorcorrecting
module errorcorrecting (
  input  [14:0] inputdata,
  output [10:0] correcteddata
);

  wire cc0, cc1, cc2, cc3, decoder_1_out3, decoder_1_out5, decoder_1_out6, decoder_1_out7, decoder_1_out9,
       decoder_1_out10, decoder_1_out11, decoder_1_out12, decoder_1_out13, decoder_1_out14, decoder_1_out15,
       xor_5_out, xor_6_out, xor_7_out, xor_8_out, xor_9_out, xor_10_out, xor_11_out, xor_12_out, xor_13_out,
       xor_14_out, xor_28_out, xor_29_out, xor_30_out, xor_31_out, xor_32_out, xor_33_out, xor_34_out,
       xor_35_out, xor_36_out, xor_37_out;
  wire [3:0] xor_1_out;

  xor xor_1 (xor_1_out[0], inputdata[0], cc0);
  xor xor_2 (xor_1_out[1], inputdata[1], cc1);
  xor xor_3 (xor_1_out[2], inputdata[3], cc2);
  xor xor_4 (xor_1_out[3], inputdata[7], cc3);
  xor xor_5 (xor_5_out, inputdata[2], inputdata[4]);
  xor xor_6 (xor_6_out, xor_5_out, inputdata[6]);
  xor xor_7 (xor_7_out, inputdata[4], inputdata[5]);
  xor xor_8 (xor_8_out, xor_7_out, inputdata[6]);
  xor xor_9 (xor_9_out, xor_6_out, inputdata[8]);
  xor xor_10 (xor_10_out, xor_8_out, inputdata[11]);
  Decoder #(.select(4)) decoder_1 (
    .out3(decoder_1_out3), .out5(decoder_1_out5), .out6(decoder_1_out6), .out7(decoder_1_out7),
    .out9(decoder_1_out9), .out10(decoder_1_out10), .out11(decoder_1_out11), .out12(decoder_1_out12),
    .out13(decoder_1_out13), .out14(decoder_1_out14), .out15(decoder_1_out15), .sel(xor_1_out));  // open: out0, out1, out2, out4, out8, en
  xor xor_11 (xor_11_out, xor_9_out, inputdata[10]);
  xor xor_12 (xor_12_out, xor_11_out, inputdata[12]);
  xor xor_13 (xor_13_out, xor_10_out, inputdata[12]);
  xor xor_14 (xor_14_out, xor_13_out, inputdata[13]);
  xor xor_15 (cc0, xor_12_out, inputdata[14]);
  xor xor_16 (cc2, xor_14_out, inputdata[14]);
  xor xor_17 (correcteddata[0], decoder_1_out3, inputdata[2]);
  xor xor_18 (correcteddata[1], decoder_1_out5, inputdata[4]);
  xor xor_19 (correcteddata[2], decoder_1_out6, inputdata[5]);
  xor xor_20 (correcteddata[3], decoder_1_out7, inputdata[6]);
  xor xor_21 (correcteddata[4], decoder_1_out9, inputdata[8]);
  xor xor_22 (correcteddata[5], decoder_1_out10, inputdata[9]);
  xor xor_23 (correcteddata[6], decoder_1_out11, inputdata[10]);
  xor xor_24 (correcteddata[7], decoder_1_out12, inputdata[11]);
  xor xor_25 (correcteddata[8], decoder_1_out13, inputdata[12]);
  xor xor_26 (correcteddata[9], decoder_1_out14, inputdata[13]);
  xor xor_27 (correcteddata[10], decoder_1_out15, inputdata[14]);
  xor xor_28 (xor_28_out, inputdata[2], inputdata[5]);
  xor xor_29 (xor_29_out, inputdata[8], inputdata[9]);
  xor xor_30 (xor_30_out, xor_28_out, inputdata[6]);
  xor xor_31 (xor_31_out, xor_30_out, inputdata[9]);
  xor xor_32 (xor_32_out, xor_29_out, inputdata[10]);
  xor xor_33 (xor_33_out, xor_32_out, inputdata[11]);
  xor xor_34 (xor_34_out, xor_31_out, inputdata[10]);
  xor xor_35 (xor_35_out, xor_34_out, inputdata[13]);
  xor xor_36 (xor_36_out, xor_33_out, inputdata[12]);
  xor xor_37 (xor_37_out, xor_36_out, inputdata[13]);
  xor xor_38 (cc1, xor_35_out, inputdata[14]);
  xor xor_39 (cc3, xor_37_out, inputdata[14]);

  // Other names for the same wires on the sheet: C[10:0] = correcteddata; cd0 = correcteddata[0];
  //   cd1 = correcteddata[1]; cd2 = correcteddata[2]; cd3 = correcteddata[3]; cd4 = correcteddata[4];
  //   cd5 = correcteddata[5]; cd6 = correcteddata[6]; cd7 = correcteddata[7]; cd8 = correcteddata[8];
  //   cd9 = correcteddata[9]; cd10 = correcteddata[10]; c0 = inputdata[0]; c1 = inputdata[1]; d0 = inputdata[2];
  //   c2 = inputdata[3]; d1 = inputdata[4]; d2 = inputdata[5]; d3 = inputdata[6]; c3 = inputdata[7];
  //   d4 = inputdata[8]; d5 = inputdata[9]; d6 = inputdata[10]; d7 = inputdata[11]; d8 = inputdata[12];
  //   d9 = inputdata[13]; d10 = inputdata[14]
endmodule
