// Logisim project 1tester.circ as structural Verilog: 1 circuit, main circuit main
module main (
  output q,
  output sysclock,
  output q1ago,
  output q2ago,
  output halt
);

  wire not_1_out;

  Clock clock_1 (.out(sysclock));
  Counter #(.width(9), .max('h1ff)) counter_1 (
    .up(1'b1), .clk(sysclock), .carry(halt));  // open: clr, load, count, D, Q
  Random #(.width(1), .seed(666)) random_1 (.next(not_1_out), .clk(sysclock), .out(q));  // open: clr
  not not_1 (not_1_out, halt);
  chaining chaining_1 (.q(q), .sysclock(sysclock), .q1ago(q1ago), .q2ago(q2ago));

  // Notes on the sheet:
  //   Place your subcircuit here.
endmodule
