// Logisim project 2.circ as structural Verilog: 1 circuit, main circuit tregister
module tregister (
  input  [7:0] eightbitinput,
  input  sysclock,
  output [7:0] registerval
);

  wire xor_1_out, xor_2_out, xor_3_out, xor_4_out, xor_5_out, xor_6_out, xor_7_out, xor_8_out;

  T_Flip_Flop t_ff_1 (.T(xor_1_out), .clk(sysclock), .Q(registerval[0]));  // open: Qn, reset, preset
  xor xor_1 (xor_1_out, registerval[0], eightbitinput[0]);
  T_Flip_Flop t_ff_2 (.T(xor_2_out), .clk(sysclock), .Q(registerval[1]));  // open: Qn, reset, preset
  xor xor_2 (xor_2_out, registerval[1], eightbitinput[1]);
  T_Flip_Flop t_ff_3 (.T(xor_3_out), .clk(sysclock), .Q(registerval[2]));  // open: Qn, reset, preset
  xor xor_3 (xor_3_out, registerval[2], eightbitinput[2]);
  T_Flip_Flop t_ff_4 (.T(xor_4_out), .clk(sysclock), .Q(registerval[3]));  // open: Qn, reset, preset
  xor xor_4 (xor_4_out, registerval[3], eightbitinput[3]);
  T_Flip_Flop t_ff_5 (.T(xor_5_out), .clk(sysclock), .Q(registerval[4]));  // open: Qn, reset, preset
  xor xor_5 (xor_5_out, registerval[4], eightbitinput[4]);
  T_Flip_Flop t_ff_6 (.T(xor_6_out), .clk(sysclock), .Q(registerval[5]));  // open: Qn, reset, preset
  xor xor_6 (xor_6_out, registerval[5], eightbitinput[5]);
  T_Flip_Flop t_ff_7 (.T(xor_7_out), .clk(sysclock), .Q(registerval[6]));  // open: Qn, reset, preset
  xor xor_7 (xor_7_out, registerval[6], eightbitinput[6]);
  T_Flip_Flop t_ff_8 (.T(xor_8_out), .clk(sysclock), .Q(registerval[7]));  // open: Qn, reset, preset
  xor xor_8 (xor_8_out, registerval[7], eightbitinput[7]);

  // Other names for the same wires on the sheet: c = sysclock; i1 = eightbitinput[0]; i2 = eightbitinput[1];
  //   i3 = eightbitinput[2]; i4 = eightbitinput[3]; i5 = eightbitinput[4]; i6 = eightbitinput[5];
  //   i7 = eightbitinput[6]; i8 = eightbitinput[7]; a1 = registerval[0]; r[7:0] = registerval; a2 = registerval[1];
  //   a3 = registerval[2]; a4 = registerval[3]; a5 = registerval[4]; a6 = registerval[5]; a7 = registerval[6];
  //   a8 = registerval[7]
endmodule
