// Logisim project 2tester.circ as structural Verilog: 1 circuit, main circuit main
module main (
  output [7:0] eightbitinput,
  output sysclock,
  output [7:0] registerval,
  output halt
);

  wire not_1_out;

  Clock clock_1 (.out(sysclock));
  not not_1 (not_1_out, halt);
  Counter #(.width(9), .max('h1ff), .ongoal("stay")) counter_1 (
    .up(1'b1), .clk(sysclock), .carry(halt));  // open: clr, load, count, D, Q
  Random #(.seed(666)) random_1 (.next(not_1_out), .clk(sysclock), .out(eightbitinput));  // open: clr
  tregister tregister_1 (.eightbitinput(eightbitinput), .sysclock(sysclock), .registerval(registerval));

  // Notes on the sheet:
  //   Place your subcircuit here.
endmodule
