// Logisim project 3.circ as structural Verilog: 1 circuit, main circuit fsmtable
module fsmtable (
  input  inputu,
  input  sysclock,
  output outputn
);

  wire and_1_out, and_2_out, and_3_out, and_4_out, and_5_out, d_ff_2_q, not_1_out, not_2_out, not_3_out,
       or_1_out, or_2_out;

  not not_1 (not_1_out, inputu);
  and and_1 (and_1_out, not_1_out, not_3_out);
  and and_2 (and_2_out, inputu, d_ff_2_q);
  or or_1 (or_1_out, and_1_out, and_2_out);
  and and_3 (and_3_out, not_3_out, not_1_out);
  or or_2 (or_2_out, and_3_out, and_4_out, and_5_out);
  and and_4 (and_4_out, not_3_out, d_ff_2_q);
  and and_5 (and_5_out, not_2_out, outputn, inputu);
  not not_2 (not_2_out, d_ff_2_q);
  not not_3 (not_3_out, outputn);
  D_Flip_Flop d_ff_1 (.D(or_1_out), .clk(sysclock), .Q(outputn));  // open: Qn, preset, reset
  D_Flip_Flop d_ff_2 (.D(or_2_out), .clk(sysclock), .Q(d_ff_2_q));  // open: Qn, preset, reset

  // Other names for the same wires on the sheet: i = inputu; o = outputn
endmodule
