// Logisim project 4.circ as structural Verilog: 1 circuit, main circuit fsmdiagram
module fsmdiagram (
  input  inputv,
  input  sysclock,
  output outputp
);

  wire and_1_out, and_2_out, and_3_out, and_4_out, and_5_out, and_6_out, and_7_out, and_8_out, and_9_out,
       and_10_out, and_11_out, and_12_out, and_13_out, and_14_out, and_15_out, d_ff_1_q, d_ff_2_q, d_ff_3_q,
       not_1_out, not_2_out, not_3_out, not_4_out, not_5_out, or_1_out, or_2_out, or_3_out;

  not not_1 (not_1_out, inputv);
  and and_1 (and_1_out, not_2_out, d_ff_3_q);
  and and_2 (and_2_out, d_ff_1_q, not_3_out);
  and and_3 (and_3_out, d_ff_1_q, d_ff_2_q, not_4_out);
  and and_4 (and_4_out, d_ff_2_q, not_4_out, inputv);
  and and_5 (and_5_out, d_ff_1_q, not_3_out);
  and and_6 (and_6_out, not_3_out, not_4_out, inputv);
  and and_7 (and_7_out, not_2_out, d_ff_2_q, not_1_out);
  and and_8 (and_8_out, not_4_out, not_1_out);
  and and_9 (and_9_out, d_ff_1_q, not_4_out);
  and and_10 (and_10_out, not_2_out, not_3_out, not_1_out);
  and and_11 (and_11_out, d_ff_1_q, not_3_out, inputv);
  and and_12 (and_12_out, not_2_out, d_ff_2_q, d_ff_3_q, inputv);
  not not_2 (not_2_out, d_ff_1_q);
  not not_3 (not_3_out, d_ff_2_q);
  not not_4 (not_4_out, d_ff_3_q);
  or or_1 (or_1_out, and_1_out, and_2_out, and_3_out, and_4_out);
  or or_2 (or_2_out, and_5_out, and_6_out, and_7_out);
  or or_3 (or_3_out, and_8_out, and_9_out, and_10_out, and_11_out, and_12_out);
  D_Flip_Flop d_ff_1 (.D(or_1_out), .clk(sysclock), .Q(d_ff_1_q));  // open: Qn, preset, reset
  D_Flip_Flop d_ff_2 (.D(or_2_out), .clk(sysclock), .Q(d_ff_2_q));  // open: Qn, preset, reset
  D_Flip_Flop d_ff_3 (.D(or_3_out), .clk(sysclock), .Q(d_ff_3_q));  // open: Qn, preset, reset
  not not_5 (not_5_out, d_ff_3_q);
  and and_13 (and_13_out, d_ff_2_q, not_5_out);
  and and_14 (and_14_out, d_ff_1_q, not_5_out);
  and and_15 (and_15_out, d_ff_1_q, d_ff_2_q);
  or or_4 (outputp, and_13_out, and_14_out, and_15_out);

  // Other names for the same wires on the sheet: o = outputp; x = inputv
endmodule
