// Logisim project 4tester.circ as structural Verilog: 1 circuit, main circuit main
module main (
  output inputv,
  output sysclock,
  output outputp,
  output halt
);

  wire not_1_out;

  Clock clock_1 (.out(sysclock));
  Counter #(.width(9), .max('h1ff), .ongoal("stay")) counter_1 (
    .up(1'b1), .clk(sysclock), .carry(halt));  // open: clr, load, count, D, Q
  Random #(.width(1), .seed(666)) random_1 (.next(not_1_out), .clk(sysclock), .out(inputv));  // open: clr
  not not_1 (not_1_out, halt);
  fsmdiagram fsmdiagram_1 (.inputv(inputv), .sysclock(sysclock), .outputp(outputp));

  // Notes on the sheet:
  //   Place your subcircuit here.
endmodule
