// Logisim project 5.circ as structural Verilog: 1 circuit, main circuit paritygen
module paritygen (
  input  inputw,
  input  sysclock,
  output outputq
);

  wire and_1_out, and_2_out, and_3_out, and_4_out, and_5_out, and_6_out, and_7_out, and_8_out, and_9_out,
       d_ff_1_q, d_ff_2_q, d_ff_3_q, not_1_out, not_2_out, not_3_out, not_4_out, not_5_out, or_1_out,
       or_2_out, or_3_out;

  not not_1 (not_1_out, inputw);
  and and_1 (and_1_out, not_2_out, d_ff_3_q, inputw);
  and and_2 (and_2_out, d_ff_2_q, not_4_out, not_1_out);
  and and_3 (and_3_out, d_ff_1_q, not_4_out, not_1_out);
  and and_4 (and_4_out, not_2_out, not_4_out, inputw);
  and and_5 (and_5_out, d_ff_1_q, d_ff_3_q, inputw);
  and and_6 (and_6_out, not_2_out, not_3_out, d_ff_3_q, not_1_out);
  and and_7 (and_7_out, d_ff_2_q, inputw);
  and and_8 (and_8_out, not_3_out, not_1_out);
  or or_1 (or_1_out, and_1_out, and_2_out, and_3_out);
  or or_2 (or_2_out, and_4_out, and_5_out, and_6_out);
  or or_3 (or_3_out, and_7_out, and_8_out);
  not not_2 (not_2_out, d_ff_1_q);
  not not_3 (not_3_out, d_ff_2_q);
  not not_4 (not_4_out, d_ff_3_q);
  D_Flip_Flop d_ff_1 (.D(or_1_out), .clk(sysclock), .Q(d_ff_1_q));  // open: Qn, preset, reset
  D_Flip_Flop d_ff_2 (.D(or_2_out), .clk(sysclock), .Q(d_ff_2_q));  // open: Qn, preset, reset
  D_Flip_Flop d_ff_3 (.D(or_3_out), .clk(sysclock), .Q(d_ff_3_q));  // open: Qn, preset, reset
  not not_5 (not_5_out, d_ff_3_q);
  and and_9 (and_9_out, d_ff_2_q, not_5_out);
  or or_4 (outputq, d_ff_1_q, and_9_out);

  // Other names for the same wires on the sheet: i = inputw; x = outputq
endmodule
