// Logisim project 7.circ as structural Verilog: 1 circuit, main circuit vendingmachine
module vendingmachine (
  input  input5,
  input  input10,
  input  input20,
  input  sysclock,
  output outputcoke,
  output output5,
  output output10
);

  wire and_1_out, and_2_out, and_3_out, and_4_out, and_5_out, and_6_out, and_7_out, and_8_out, and_9_out,
       and_10_out, and_11_out, and_12_out, and_13_out, and_14_out, and_15_out, and_16_out, and_17_out,
       and_18_out, and_19_out, and_20_out, and_21_out, and_22_out, and_23_out, and_24_out, and_25_out,
       and_26_out, and_27_out, and_28_out, d_ff_1_q, d_ff_1_qn, d_ff_2_q, d_ff_2_qn, d_ff_3_q, d_ff_3_qn,
       not_1_out, not_2_out, not_3_out, or_1_out, or_2_out, or_3_out;

  not not_1 (not_1_out, input5);
  not not_2 (not_2_out, input10);
  not not_3 (not_3_out, input20);
  and and_1 (and_1_out, d_ff_1_qn, d_ff_3_q, input5);
  and and_2 (and_2_out, d_ff_1_qn, d_ff_2_q, input10);
  and and_3 (and_3_out, d_ff_2_q, d_ff_3_qn, input10);
  and and_4 (and_4_out, d_ff_2_q, d_ff_3_q, input5);
  and and_5 (and_5_out, d_ff_1_qn, d_ff_2_qn, d_ff_3_q, input20);
  and and_6 (and_6_out, d_ff_1_qn, d_ff_2_q, d_ff_3_qn, input20);
  and and_7 (and_7_out, d_ff_1_q, not_1_out, not_2_out, not_3_out);
  and and_8 (and_8_out, d_ff_1_qn, d_ff_3_qn, input20);
  and and_9 (and_9_out, d_ff_1_qn, d_ff_2_qn, input5);
  and and_10 (and_10_out, d_ff_1_qn, d_ff_3_q, input5);
  and and_11 (and_11_out, d_ff_2_q, d_ff_3_qn, input10);
  and and_12 (and_12_out, d_ff_1_q, d_ff_3_qn, not_3_out);
  and and_13 (and_13_out, d_ff_2_q, not_1_out, not_2_out, not_3_out);
  and and_14 (and_14_out, d_ff_1_qn, d_ff_2_qn, d_ff_3_q, input10);
  and and_15 (and_15_out, d_ff_2_q, input5);
  and and_16 (and_16_out, d_ff_1_qn, d_ff_2_qn, input20);
  and and_17 (and_17_out, d_ff_1_qn, d_ff_3_qn, input20);
  and and_18 (and_18_out, d_ff_1_qn, d_ff_2_qn, input10);
  and and_19 (and_19_out, d_ff_1_qn, d_ff_3_q, input10);
  and and_20 (and_20_out, d_ff_1_q, d_ff_3_qn, input10);
  and and_21 (and_21_out, d_ff_3_q, not_1_out, not_2_out, not_3_out);
  D_Flip_Flop d_ff_1 (.D(or_1_out), .clk(sysclock), .Q(d_ff_1_q), .Qn(d_ff_1_qn));  // open: preset, reset
  or or_1 (or_1_out, and_1_out, and_2_out, and_3_out, and_4_out, and_5_out, and_6_out, and_7_out);
  D_Flip_Flop d_ff_2 (.D(or_2_out), .clk(sysclock), .Q(d_ff_2_q), .Qn(d_ff_2_qn));  // open: preset, reset
  or or_2 (or_2_out, and_8_out, and_9_out, and_10_out, and_11_out, and_12_out, and_13_out, and_14_out);
  D_Flip_Flop d_ff_3 (.D(or_3_out), .clk(sysclock), .Q(d_ff_3_q), .Qn(d_ff_3_qn));  // open: preset, reset
  or or_3 (or_3_out, and_15_out, and_16_out, and_17_out, and_18_out, and_19_out, and_20_out, and_21_out);
  and and_22 (and_22_out, d_ff_1_q, input20);
  and and_23 (and_23_out, d_ff_2_q, d_ff_3_q, input20);
  and and_24 (and_24_out, d_ff_1_q, d_ff_2_qn, input5);
  and and_25 (and_25_out, d_ff_1_q, d_ff_3_q, input10);
  and and_26 (and_26_out, d_ff_1_q, d_ff_2_qn, input20);
  and and_27 (and_27_out, d_ff_1_q, d_ff_2_qn, input10);
  and and_28 (and_28_out, d_ff_1_qn, d_ff_2_q, d_ff_3_q, input20);
  and and_29 (output10, d_ff_1_q, d_ff_3_q, input20);
  or or_4 (outputcoke, and_22_out, and_23_out, and_24_out, and_25_out);
  or or_5 (output5, and_26_out, and_27_out, and_28_out);

  // Other names for the same wires on the sheet: i5 = input5; i10 = input10; i20 = input20; x5 = output5;
  //   x10 = output10; xc = outputcoke
endmodule
