// Logisim project 7tester.circ as structural Verilog: 1 circuit, main circuit main
module main (
  output input5,
  output input10,
  output input20,
  output sysclock,
  output outputcoke,
  output output5,
  output output10,
  output halt
);

  wire not_1_out;
  wire [1:0] random_1_out;

  Clock clock_1 (.out(sysclock));
  Counter #(.width(9), .max('h1ff), .ongoal("stay")) counter_1 (
    .up(1'b1), .clk(sysclock), .carry(halt));  // open: clr, load, count, D, Q
  not not_1 (not_1_out, halt);
  Random #(.width(2), .seed(666)) random_1 (.next(not_1_out), .clk(sysclock), .out(random_1_out));  // open: clr
  Decoder #(.select(2), .enable("false")) decoder_1 (
    .out1(input5), .out2(input10), .out3(input20), .sel(random_1_out));  // open: out0
  vendingmachine vendingmachine_1 (
    .input5(input5), .input10(input10), .input20(input20), .sysclock(sysclock), .outputcoke(outputcoke),
    .output5(output5), .output10(output10));

  // Notes on the sheet:
  //   Place your subcircuit here.
endmodule
