// Logisim project 1.circ as structural Verilog: 1 circuit, main circuit alu8
module alu8 (
  input  [7:0] a,
  input  [7:0] b,
  input  [3:0] op,
  output [7:0] rddata
);

  wire and_10_out, and_11_out, and_12_out, and_13_out, and_14_out, and_15_out, and_16_out, and_17_out,
       and_18_out, and_19_out, and_20_out, and_21_out, and_22_out, and_23_out, and_24_out, and_25_out,
       and_26_out, and_27_out, and_28_out, and_29_out, C0, C4, comparator_1_eq, G0, G1, G2, G3, G4, G5, G6,
       G7, or_3_out, or_4_out, or_5_out, or_6_out, or_7_out, or_8_out, or_9_out, P0, P1, P2, P3, P4, P5, P6,
       P7, xor_2_out, xor_3_out, xor_4_out, xor_5_out, xor_6_out, xor_7_out, xor_8_out, xor_9_out;
  wire [7:0] ADD, and_1_out, multiplexer_1_out, not_1_out, or_1_out, shifter_1_out, shifter_2_out, xor_1_out;

  assign not_1_out = ~a;  // NOT_Gate not_1, 8 bits wide
  assign and_1_out = a & b;  // AND_Gate and_1, 8 bits wide
  assign xor_1_out = a ^ b;  // XOR_Gate xor_1, 8 bits wide
  assign or_1_out = a | b;  // OR_Gate or_1, 8 bits wide
  Shifter shifter_1 (.in(a), .\dist (3'b001), .out(shifter_1_out));
  Shifter #(.shift("lr")) shifter_2 (.in(a), .\dist (3'b001), .out(shifter_2_out));
  xor xor_2 (xor_2_out, b[0], C0);
  xor xor_3 (xor_3_out, b[1], C0);
  xor xor_4 (xor_4_out, b[2], C0);
  xor xor_5 (xor_5_out, b[3], C0);
  xor xor_6 (xor_6_out, b[4], C0);
  xor xor_7 (xor_7_out, b[5], C0);
  xor xor_8 (xor_8_out, b[6], C0);
  xor xor_9 (xor_9_out, b[7], C0);
  Multiplexer #(.width(8), .enable("false")) multiplexer_1 (
    .in0({8{1'b0}}), .in1(8'h1), .out(multiplexer_1_out), .sel(comparator_1_eq));
  Comparator comparator_1 (.a(b), .b(a), .eq(comparator_1_eq));  // open: gt, lt
  and and_2 (G0, a[0], xor_2_out);
  xor xor_10 (P0, a[0], xor_2_out);
  and and_3 (G1, a[1], xor_3_out);
  xor xor_11 (P1, a[1], xor_3_out);
  and and_4 (G2, a[2], xor_4_out);
  xor xor_12 (P2, a[2], xor_4_out);
  and and_5 (G3, a[3], xor_5_out);
  xor xor_13 (P3, a[3], xor_5_out);
  and and_6 (G4, a[4], xor_6_out);
  xor xor_14 (P4, a[4], xor_6_out);
  and and_7 (G5, a[5], xor_7_out);
  xor xor_15 (P5, a[5], xor_7_out);
  and and_8 (G6, a[6], xor_8_out);
  xor xor_16 (P6, a[6], xor_8_out);
  and and_9 (G7, a[7], xor_9_out);
  xor xor_17 (P7, a[7], xor_9_out);
  and and_10 (and_10_out, G2, P3);
  and and_11 (and_11_out, G1, P2, P3);
  and and_12 (and_12_out, G0, P1, P2, P3);
  and and_13 (and_13_out, C0, P0, P1, P2, P3);
  Multiplexer #(.select(4), .enable("false")) multiplexer_2 (
    .in5(1'b0), .in6(1'b1), .in9(1'b0), .in10(1'b1), .out(C0), .sel(op));  // open: in0, in1, in2, in3, in4, in7, in8, in11, in12, in13, in14, in15
  Multiplexer #(.select(4), .width(8), .enable("false")) multiplexer_3 (
    .in1(not_1_out), .in2(and_1_out), .in3(xor_1_out), .in4(or_1_out), .in5(ADD), .in6(ADD), .in7(a),
    .in8(b), .in9(ADD), .in10(ADD), .in11(shifter_1_out), .in12(shifter_2_out), .in13(multiplexer_1_out),
    .out(rddata), .sel(op));  // open: in0, in14, in15
  or or_2 (C4, G3, and_10_out, and_11_out, and_12_out, and_13_out);
  xor xor_18 (ADD[0], P0, C0);
  and and_14 (and_14_out, C0, P0);
  and and_15 (and_15_out, G0, P1);
  and and_16 (and_16_out, C0, P0, P1);
  and and_17 (and_17_out, G1, P2);
  and and_18 (and_18_out, G0, P1, P2);
  and and_19 (and_19_out, C0, P0, P1, P2);
  and and_20 (and_20_out, G2, P3);
  and and_21 (and_21_out, G1, P2, P3);
  and and_22 (and_22_out, G0, P1, P2, P3);
  and and_23 (and_23_out, C0, P0, P1, P2, P3);
  xor xor_19 (ADD[1], P1, or_3_out);
  or or_3 (or_3_out, G0, and_14_out);
  xor xor_20 (ADD[2], P2, or_4_out);
  or or_4 (or_4_out, G1, and_15_out, and_16_out);
  or or_5 (or_5_out, G2, and_17_out, and_18_out, and_19_out);
  or or_6 (or_6_out, G3, and_20_out, and_21_out, and_22_out, and_23_out);
  xor xor_21 (ADD[3], P3, or_5_out);
  xor xor_22 (ADD[4], P4, or_6_out);
  and and_24 (and_24_out, C4, P4);
  and and_25 (and_25_out, G4, P5);
  and and_26 (and_26_out, C4, P4, P5);
  and and_27 (and_27_out, G5, P6);
  and and_28 (and_28_out, G4, P5, P6);
  and and_29 (and_29_out, C4, P4, P5, P6);
  or or_7 (or_7_out, G4, and_24_out);
  or or_8 (or_8_out, G5, and_25_out, and_26_out);
  or or_9 (or_9_out, G6, and_27_out, and_28_out, and_29_out);
  xor xor_23 (ADD[5], P5, or_7_out);
  xor xor_24 (ADD[6], P6, or_8_out);
  xor xor_25 (ADD[7], P7, or_9_out);

  // Other names for the same wires on the sheet: S0 = ADD[0]; SUB[7:0] = ADD; S1 = ADD[1]; S2 = ADD[2]; S3 = ADD[3];
  //   S4 = ADD[4]; S5 = ADD[5]; S6 = ADD[6]; S7 = ADD[7]
endmodule
