// Logisim project 1tester.circ as structural Verilog: 1 circuit, main circuit main
module main (
  output [7:0] a,
  output [7:0] b,
  output [3:0] op,
  output [7:0] rddata,
  output halt
);

  wire catchfire, sysclock;
  wire [3:0] random_1_out;

  Clock clock_1 (.out(sysclock));
  Counter #(.ongoal("stay")) counter_1 (.up(1'b1), .clk(sysclock), .carry(halt));  // open: clr, load, count, D, Q
  not not_1 (catchfire, halt);
  Random #(.width(20), .seed(666)) random_1 (
    .next(catchfire), .clk(sysclock), .out({a, b, random_1_out}));  // open: clr
  Multiplexer #(.select(4), .width(4), .enable("false")) multiplexer_1 (
    .in0(4'b0101), .in1(random_1_out), .in2(random_1_out), .in3(random_1_out), .in4(random_1_out),
    .in5(random_1_out), .in6(random_1_out), .in7(random_1_out), .in8(random_1_out), .in9(random_1_out),
    .in10(random_1_out), .in11(random_1_out), .in12(random_1_out), .in13(random_1_out), .in14(4'b0110),
    .in15(4'b1001), .out(op), .sel(random_1_out));
  alu8 alu8_1 (.a(a), .b(b), .op(op), .rddata(rddata));

  // Notes on the sheet:
  //   Place your subcircuit here.
endmodule
