// Logisim project 2tester.circ as structural Verilog: 1 circuit, main circuit main
module main (
  output resetall,
  output sysclock,
  output [7:0] pc,
  output [3:0] op,
  output [2:0] rd,
  output [2:0] rs1,
  output [2:0] rs2,
  output [7:0] imm,
  output halt
);

  wire catchfire;
  wire [8:0] counter_1_q;

  Clock clock_1 (.out(sysclock));
  Counter #(.width(9), .max('h1ff), .ongoal("stay")) counter_1 (
    .up(1'b1), .clk(sysclock), .carry(halt), .Q(counter_1_q));  // open: clr, load, count, D
  not not_1 (catchfire, halt);
  Comparator #(.width(9)) comparator_1 (.a(counter_1_q), .b(9'hff), .eq(resetall));  // open: gt, lt
  instructions instructions_1 (
    .resetall(resetall), .sysclock(sysclock), .pc(pc), .op(op), .rd(rd), .rs1(rs1), .rs2(rs2), .imm(imm));

  // Notes on the sheet:
  //   Place your subcircuit here.
endmodule
