// Logisim project 3.circ as structural Verilog: 1 circuit, main circuit regfile
module regfile (
  input  [2:0] rd,
  input  [7:0] rddata,
  input  wen,
  input  resetall,
  input  sysclock,
  output [7:0] x0,
  output [7:0] x1,
  output [7:0] x2,
  output [7:0] x3,
  output [7:0] x4,
  output [7:0] x5,
  output [7:0] x6,
  output [7:0] x7
);

  wire decoder_1_out0, decoder_1_out1, decoder_1_out2, decoder_1_out3, decoder_1_out4, decoder_1_out5,
       decoder_1_out6, decoder_1_out7;

  Decoder #(.select(3)) decoder_1 (
    .out0(decoder_1_out0), .out1(decoder_1_out1), .out2(decoder_1_out2), .out3(decoder_1_out3),
    .out4(decoder_1_out4), .out5(decoder_1_out5), .out6(decoder_1_out6), .out7(decoder_1_out7), .sel(rd),
    .en(wen));
  Register register_1 (.D(rddata), .en(decoder_1_out0), .clk(sysclock), .Q(x0), .clr(resetall));
  Register register_2 (.D(rddata), .en(decoder_1_out1), .clk(sysclock), .Q(x1), .clr(resetall));
  Register register_3 (.D(rddata), .en(decoder_1_out2), .clk(sysclock), .Q(x2), .clr(resetall));
  Register register_4 (.D(rddata), .en(decoder_1_out3), .clk(sysclock), .Q(x3), .clr(resetall));
  Register register_5 (.D(rddata), .en(decoder_1_out4), .clk(sysclock), .Q(x4), .clr(resetall));
  Register register_6 (.D(rddata), .en(decoder_1_out5), .clk(sysclock), .Q(x5), .clr(resetall));
  Register register_7 (.D(rddata), .en(decoder_1_out6), .clk(sysclock), .Q(x6), .clr(resetall));
  Register register_8 (.D(rddata), .en(decoder_1_out7), .clk(sysclock), .Q(x7), .clr(resetall));
endmodule
