// Logisim project 3tester.circ as structural Verilog: 1 circuit, main circuit main
module main (
  output [2:0] rd,
  output [7:0] rddata,
  output wen,
  output resetall,
  output sysclock,
  output [7:0] x0,
  output [7:0] x1,
  output [7:0] x2,
  output [7:0] x3,
  output [7:0] x4,
  output [7:0] x5,
  output [7:0] x6,
  output [7:0] x7,
  output halt
);

  wire catchfire;
  wire [1:0] random_1_out;
  wire [8:0] counter_1_q;

  Clock clock_1 (.out(sysclock));
  Counter #(.width(9), .max('h1ff), .ongoal("stay")) counter_1 (
    .up(1'b1), .clk(sysclock), .carry(halt), .Q(counter_1_q));  // open: clr, load, count, D
  Random #(.width(13), .seed(666)) random_1 (
    .next(catchfire), .clk(sysclock), .out({rddata, rd, random_1_out}));  // open: clr
  not not_1 (catchfire, halt);
  Comparator #(.width(9), .mode("unsigned")) comparator_1 (.a(counter_1_q), .b(9'hff), .eq(resetall));  // open: gt, lt
  Multiplexer #(.select(2), .enable("false")) multiplexer_1 (
    .in0(1'b1), .in1(1'b1), .in2(1'b1), .in3(1'b0), .out(wen), .sel(random_1_out));
  regfile regfile_1 (
    .rd(rd), .rddata(rddata), .wen(wen), .resetall(resetall), .sysclock(sysclock), .x0(x0), .x1(x1), .x2(x2),
    .x3(x3), .x4(x4), .x5(x5), .x6(x6), .x7(x7));

  // Notes on the sheet:
  //   Place your subcircuit here.
endmodule
