// Logisim project 4tester.circ as structural Verilog: 1 circuit, main circuit main
module main (
  output resetall,
  output sysclock,
  output [7:0] pc,
  output [7:0] x0,
  output [7:0] x1,
  output [7:0] x2,
  output [7:0] x3,
  output [7:0] x4,
  output [7:0] x5,
  output [7:0] x6,
  output [7:0] x7,
  output halt
);

  wire catchfire;

  Clock clock_1 (.out(sysclock));
  Counter #(.ongoal("stay")) counter_1 (.up(1'b1), .clk(sysclock), .carry(halt));  // open: clr, load, count, D, Q
  not not_1 (catchfire, halt);
  cpu cpu_1 (
    .resetall(1'b0), .sysclock(sysclock), .pc(pc), .x0(x0), .x1(x1), .x2(x2), .x3(x3), .x4(x4), .x5(x5),
    .x6(x6), .x7(x7));

  assign resetall = 1'b0;

  // Notes on the sheet:
  //   Place your subcircuit here.
endmodule
