// Logisim project extracredit.circ as structural Verilog: 1 circuit, main circuit ledger
module ledger (
  input  [2:0] customerid,
  input  [1:0] transactiontype,
  input  [7:0] transactionamount,
  input  sysclock,
  output [1:0] transactionresult,
  output [7:0] amountremaining
);

  wire add1, decoder_1_out0, decoder_1_out1, decoder_1_out2, decoder_1_out3, decoder_1_out4, decoder_1_out5,
       decoder_1_out6, decoder_1_out7, not_1_out, not_2_out, sub1;
  wire [1:0] multiplexer_1_out, multiplexer_2_out;
  wire [7:0] add, input14, multiplexer_3_out, multiplexer_4_out, register_1_q, register_2_q, register_3_q,
       register_4_q, register_5_q, register_6_q, register_7_q, register_8_q, remain1, remain2, sub;

  Multiplexer #(.width(2), .enable("false")) multiplexer_1 (
    .in0(2'b01), .in1(2'b10), .out(multiplexer_1_out), .sel(add1));
  Multiplexer #(.width(2), .enable("false")) multiplexer_2 (
    .in0(2'b11), .in1(2'b01), .out(multiplexer_2_out), .sel(not_1_out));
  not not_1 (not_1_out, sub1);
  Adder adder_1 (.a(remain1), .b(transactionamount), .out(add), .cin(1'b0), .cout(add1));
  Multiplexer #(.width(8), .enable("false")) multiplexer_3 (
    .in0(add), .in1(remain1), .out(multiplexer_3_out), .sel(add1));
  Multiplexer #(.width(8), .enable("false")) multiplexer_4 (
    .in0(remain1), .in1(sub), .out(multiplexer_4_out), .sel(not_2_out));
  not not_2 (not_2_out, sub1);
  Multiplexer #(.select(2), .width(2), .enable("false")) multiplexer_5 (
    .in0(2'b00), .in1(multiplexer_1_out), .in2(multiplexer_2_out), .in3(2'b00), .out(transactionresult),
    .sel(transactiontype));
  Multiplexer #(.select(2), .width(8), .enable("false")) multiplexer_6 (
    .in0(remain1), .in1(remain2), .in2(remain2), .in3(remain1), .out(amountremaining), .sel(transactiontype));
  Multiplexer #(.select(2), .width(8), .enable("false")) multiplexer_7 (
    .in0(remain1), .in1(multiplexer_3_out), .in2(multiplexer_4_out), .in3(remain1), .out(input14),
    .sel(transactiontype));
  Subtractor subtractor_1 (.a(remain1), .b(transactionamount), .out(sub), .bin(1'b0), .bout(sub1));
  Multiplexer #(.select(3), .width(8), .enable("false")) multiplexer_8 (
    .in0(input14), .in1(input14), .in2(input14), .in3(input14), .in4(input14), .in5(input14), .in6(input14),
    .in7(input14), .out(remain2), .sel(customerid));
  Decoder #(.select(3)) decoder_1 (
    .out0(decoder_1_out0), .out1(decoder_1_out1), .out2(decoder_1_out2), .out3(decoder_1_out3),
    .out4(decoder_1_out4), .out5(decoder_1_out5), .out6(decoder_1_out6), .out7(decoder_1_out7),
    .sel(customerid), .en(1'b1));
  Register register_1 (.D(input14), .en(decoder_1_out0), .clk(sysclock), .Q(register_1_q), .clr(1'b0));
  Register register_2 (.D(input14), .en(decoder_1_out1), .clk(sysclock), .Q(register_2_q), .clr(1'b0));
  Register register_3 (.D(input14), .en(decoder_1_out2), .clk(sysclock), .Q(register_3_q), .clr(1'b0));
  Register register_4 (.D(input14), .en(decoder_1_out3), .clk(sysclock), .Q(register_4_q), .clr(1'b0));
  Register register_5 (.D(input14), .en(decoder_1_out4), .clk(sysclock), .Q(register_5_q), .clr(1'b0));
  Register register_6 (.D(input14), .en(decoder_1_out5), .clk(sysclock), .Q(register_6_q), .clr(1'b0));
  Register register_7 (.D(input14), .en(decoder_1_out6), .clk(sysclock), .Q(register_7_q), .clr(1'b0));
  Register register_8 (.D(input14), .en(decoder_1_out7), .clk(sysclock), .Q(register_8_q), .clr(1'b0));
  Multiplexer #(.select(3), .width(8), .enable("false")) multiplexer_9 (
    .in0(register_1_q), .in1(register_2_q), .in2(register_3_q), .in3(register_4_q), .in4(register_5_q),
    .in5(register_6_q), .in6(register_7_q), .in7(register_8_q), .out(remain1), .sel(customerid));

  // Other names for the same wires on the sheet: clock = sysclock; id[2:0] = customerid; remain3[7:0] = remain2;
  //   remain4[7:0] = remain1; result[1:0] = transactionresult; tp[1:0] = transactiontype;
  //   transaction[7:0] = transactionamount
endmodule
