// Logisim project extracredittester.circ as structural Verilog: 1 circuit, main circuit main
module main (
  output [2:0] customerid,
  output [1:0] transactiontype,
  output [7:0] transactionamount,
  output sysclock,
  output [1:0] transactionresult,
  output [7:0] amountremaining,
  output halt
);

  wire not_1_out;
  wire [1:0] multiplexer_1_out;
  wire [7:0] counter_1_q;
  wire [12:0] random_1_out, rom_1_data;

  Clock clock_1 (.out(sysclock));
  Counter #(.ongoal("stay")) counter_1 (
    .up(1'b1), .clk(sysclock), .carry(halt), .Q(counter_1_q));  // open: clr, load, count, D
  not not_1 (not_1_out, halt);
  ROM #(.dataWidth(13)) rom_1 (.addr(counter_1_q), .data(rom_1_data));
  Random #(.width(13), .seed(666)) random_1 (.next(not_1_out), .clk(sysclock), .out(random_1_out));  // open: clr
  Multiplexer #(.select(2), .width(2), .enable("false")) multiplexer_1 (
    .in0(random_1_out[9:8]), .in1(random_1_out[9:8]), .in2(random_1_out[9:8]), .in3(2'b00),
    .out(multiplexer_1_out), .sel(random_1_out[9:8]));
  Multiplexer #(.width(13), .enable("false")) multiplexer_2 (
    .in0({random_1_out[12:10], multiplexer_1_out, random_1_out[7:0]}), .in1(rom_1_data),
    .out({customerid, transactiontype, transactionamount}), .sel(1'b0));
  ledger ledger_1 (
    .customerid(customerid), .transactiontype(transactiontype), .transactionamount(transactionamount),
    .sysclock(sysclock), .transactionresult(transactionresult), .amountremaining(amountremaining));

  // Notes on the sheet:
  //   contents of rom_1 (hex, n*v repeats v):
  //   110 510 910 d10 1110 1510 1910 1d10 ff 4ff 8ff cff 10ff 14ff 18ff 1cff 220 620 a20 e20 1220 1620
  //   1a20 1e20 1ff 5ff 9ff dff 11ff 15ff 19ff 1dff 110 510 910 d10 1110 1510 1910 1d10 ff 4ff 8ff cff
  //   10ff 14ff 18ff 1cff 220 620 a20 e20 1220 1620 1a20 1e20 ff 4ff 8ff cff 10ff 14ff 18ff 1cff
  //   0 for random tester, 1 for ram/extracredit.txt
  //   Place your subcircuit here.
endmodule
